# Fritzing sketch Macchina (saved by Fritzing 0.9.3b)
breadboards: 1

parts:
  S1 = H-Bridge with L298N
  S2 = H-Bridge with L298N
  Componente1 = Arduino Mega ADK (Rev3)
  IR1 = 4 IR obstacle detector FC-35
  M1 = fc-51 [package=THT]  # not connected
  VCC1 = Battery
  M4 = DC Motor
  M5 = DC Motor
  M6 = fc-51 [package=THT]  # not connected
  M7 = fc-51 [package=THT]  # not connected
  M8 = fc-51 [package=THT]  # not connected
  M10 = DC Motor
  M11 = DC Motor
  NRF24L1 = NRF24L01
  Componente2 = SRF05 Ultrasonic Rangefinder
  Componente3 = Bluetooth HC-05 Macho
  VCC2 = Battery block 9V  # not connected
  R1 = Resistor [tolerance=±5% resistance=2.2k package="0805 [SMD]"]
  R2 = Resistor [tolerance=±5% resistance=1k package="0805 [SMD]"]
  R3 = Resistor [tolerance=±5% resistance=10 package="0805 [SMD]"]

nets:
  12V: S1.12V, S2.12V, R3.Pin_1
  GND: S1.GND, S2.GND, VCC1.-, R1.Pin_0
  N1: S1.ENA, Componente1.D6_PWM
  N2: S1.IN1, Componente1.D30
  N3: S1.IN2, Componente1.D32
  N4: S1.IN3, Componente1.D34
  N5: S1.IN4, Componente1.D36
  N6: S1.ENB, Componente1.D9_PWM
  N7: S1.M1-01, M4.pin_2
  N8: S1.M1-02, M4.pin_1
  N9: S1.M2-01, M5.pin_2
  N10: S1.M2-02, M5.pin_1
  N11: S2.ENA, Componente1.D5_PWM
  N12: S2.IN1, Componente1.D22
  N13: S2.IN2, Componente1.D24
  N14: S2.IN3, Componente1.D26
  N15: S2.IN4, Componente1.D28
  N16: S2.ENB, Componente1.D3_PWM
  N17: S2.M1-01, M10.pin_2
  N18: S2.M1-02, M10.pin_1
  N19: S2.M2-01, M11.pin_2
  N20: S2.M2-02, M11.pin_1
  N21: Componente1.D13_PWM, IR1.D01
  N22: Componente1.D12_PWM, IR1.D02
  N23: Componente1.D11_PWM, IR1.D03
  N24: Componente1.D10_PWM, IR1.D04
  N25: Componente1.D8_PWM, Componente2.Echo
  3V3: Componente1.3V3, NRF24L1.VCC
  VCC: Componente1.5V, IR1.Vcc, Componente2.VCC, Componente3.VCC
  GND_2: Componente1.GND, IR1.GND, NRF24L1.GND, Componente2.GND, Componente3.GND
  N26: Componente1.D0/RX0, Componente3.TXD
  N27: Componente1.D1/TX0, R2.Pin_1
  N28: Componente1.D7_PWM, Componente2.Trig
  N29: Componente1.D49, NRF24L1.CE
  N30: Componente1.D50/MISO, NRF24L1.MISO
  N31: Componente1.D51/MOSI, NRF24L1.MOSI
  N32: Componente1.D52/SCK, NRF24L1.SCK
  N33: Componente1.D53/SS, NRF24L1.CSN
  N34: VCC1.+, R3.Pin_0
  N35: Componente3.RXD, R1.Pin_1, R2.Pin_0

custom parts:
  H-Bridge with L298N: h-bridge
  4 IR obstacle detector FC-35: Detector de obstáculos IR
  Battery: Your standard 2x 18650 battery pack (7,4 Volts)
  NRF24L01: NRF24L01 module
