# Fritzing sketch Semaforo (saved by Fritzing 0.9.3b)
breadboards: 1

parts:
  VCC1 = Battery block 9V  # not connected
  Componente1 = NRF24L01+ Breakout Board
  LED3 = LED - 3mm [color="Green (570nm)" package="3 mm [THT]"]
  LED2 = LED - 3mm [color="Yellow (595nm)" package="3 mm [THT]"]
  LED1 = LED - 3mm [color="Red (633nm)" package="3 mm [THT]"]
  LED4 = LED - 3mm [color="Blue (525nm)" package="3 mm [THT]"]
  R2 = Resistor [tolerance=±5% resistance=220 package="1206 [SMD]"]
  R3 = Resistor [tolerance=±5% resistance=220 package="1206 [SMD]"]
  R4 = Resistor [tolerance=±5% resistance=220 package="1206 [SMD]"]
  R5 = Resistor [tolerance=±5% resistance=10k package="1206 [SMD]"]
  Componente2 = Arduino Mega ADK (Rev3)
  hc-sr1 = hc-sr04
  hc-sr2 = hc-sr04

nets:
  GND: Componente1.GND, LED3.anode, LED2.anode, LED1.anode, LED4.anode, Componente2.GND, hc-sr1.GND, hc-sr2.GND
  VCC: Componente1.VCC, Componente2.IOREF, Componente2.5V, hc-sr1.VCC, hc-sr2.VCC
  N1: Componente1.CE, Componente2.D7_PWM
  N2: Componente1.CS, Componente2.D8_PWM
  N3: Componente1.SCK, Componente2.D52/SCK
  N4: Componente1.MOSI, Componente2.D51/MOSI
  N5: Componente1.MISO, Componente2.D50/MISO
  N6: LED3.cathode, R2.Pin_1
  N7: LED2.cathode, R3.Pin_1
  N8: LED1.cathode, R4.Pin_1
  N9: LED4.cathode, R5.Pin_1
  N10: R2.Pin_0, Componente2.D6_PWM
  N11: R3.Pin_0, Componente2.D5_PWM
  N12: R4.Pin_0, Componente2.D4_PWM
  N13: R5.Pin_0, Componente2.D3_PWM
  N14: Componente2.D46, hc-sr2.Trig
  N15: Componente2.D47, hc-sr2.Echo
  N16: Componente2.D48, hc-sr1.Trig
  N17: Componente2.D49, hc-sr1.Echo
